# Fritzing sketch parts541651 (saved by Fritzing 0.9.2b)
circuit board: 6.88566cm x 5.36311cm
breadboards: 1

parts:
  Part1 = FDC2214 [chip_label=IC package="WQFN (RGH 16)"]

nets:
  GND: Part1.1, Part1.8

custom parts:
  FDC2214: Capacitive sensing is a low-power, low-cost, high-resolution contactless sensing technique that can be applied to a variety of applications ranging from proximity detection and gesture recognition to remote liquid level sensing.
