# Fritzing sketch FDC1004_4Ch_groundplane (saved by Fritzing 0.9.2b)
circuit board: 5.27612cm x 5.46176cm
breadboards: 1

parts:
  CDC = FDC1004 [chip_label=FDC1004 package=VSSOP10]
  Part3 = Arduino Uno (Rev3)
  Ch_1 = SMA [package=SMA]
  Ch_3 = SMA [package=SMA]
  Ch_0 = SMA [package=SMA]
  Ch_2 = SMA [package=SMA]
  C1 = Ceramic Capacitor [capacitance=100nF package="1206 [SMD, multilayer]"]
  C2 = Tantalum Capacitor [capacitance=1μF package="A 3216 [SMD, tantalum]"]
  R1 = Resistor [tolerance=±5% resistance=10k package="1206 [SMD]"]
  R2 = Resistor [tolerance=±5% resistance=10k package="1206 [SMD]"]
  I2C = female pin header, 2 pins [form="♀ (female)"]
  Reset = Pushbutton [package="[THT]"]
  SPI = female pin header, 5 pins [form="♀ (female)"]
  HTU21D = HTU21D [form="♀ (female)" package=THT]
  C8 = Ceramic Capacitor [capacitance=100nF package="1206 [SMD, multilayer]"]
  SEC_GND = screw terminal, 5 pins
  filt = Resistor [tolerance=±5% resistance=0 package="1206 [SMD]"]

nets:
  GND: CDC.1, Ch_1.GND, Ch_3.GND, Ch_0.GND, Ch_2.GND
  N1: CDC.2, Ch_0.OUT
  N2: CDC.3, Ch_1.OUT
  N3: CDC.4, Ch_2.OUT
  N4: CDC.5, Ch_3.OUT
  GND_2: CDC.7, Part3.GND, C1.1, C2.-, Reset.Pin_3, Reset.Pin_4, HTU21D.GND, C8.1, SEC_GND.pin1, SEC_GND.pin2, SEC_GND.pin3, SEC_GND.pin4, SEC_GND.pin5
  N5: CDC.8, filt.Pin_0
  N6: CDC.9, Part3.A5/SCL, R1.Pin_1, I2C.pin1, HTU21D.SCK
  N7: CDC.10, Part3.A4/SDA, R2.Pin_1, I2C.pin2, HTU21D.DATA
  N8: Part3.D9_PWM, SPI.pin1
  N9: Part3.D10_PWM/SS, SPI.pin2
  N10: Part3.D11_PWM/MOSI, SPI.pin3
  N11: Part3.D12/MISO, SPI.pin4
  N12: Part3.D13/SCK, SPI.pin5
  N13: Part3.RESET, Reset.Pin_1, Reset.Pin_2
  3V3: Part3.3V3, C1.0, C2.+, R1.Pin_0, R2.Pin_0, HTU21D.VDD, C8.0, filt.Pin_1

notes:
  SCL
  SDA
  SCK
  MISO
  MOSI
  SS
  LDAC
  Austin Downey
  MAY 2016 - 4Ch CapDAQ
  0.0.0.4a
  Ground

custom parts:
  FDC1004: Capacitive sensing with grounded capacitor sensors
  SMA: TE Connectivity AMP Connectors 5-1814832-1
  HTU21D: The HTU21D(F) is a new digital humidity sensor with temperature output by MEAS. Setting new standards in terms of size and intelligence, it is embedded in a reflow solderable Dual Flat No leads (DFN) package with a small 3 x 3 x 0.9 mm footprint. This sensor provides calibrated, linearized signals in digital, I²C format.
