# Fritzing sketch FDC1004_4Ch (saved by Fritzing 0.9.2b)
circuit board: 6.88566cm x 5.36311cm
breadboards: 1

parts:
  A_OUT = Locking shrouded header - 10 pins - AMP [form="♂ (shrouded male)" package=THT]
  CDC = FDC1004 [chip_label=FDC1004 package=VSSOP10]
  DAC = MAX5134 [chip_label="MAX 5134" package=TSSOP16]
  Part3 = Arduino Uno (Rev3)
  Ch_1 = SMA [package=SMA]
  Ch_3 = SMA [package=SMA]
  Ch_0 = SMA [package=SMA]
  Ch_2 = SMA [package=SMA]
  C1 = Ceramic Capacitor [capacitance=100nF package="1206 [SMD, multilayer]"]
  C2 = Tantalum Capacitor [capacitance=1μF package="A 3216 [SMD, tantalum]"]
  R1 = Resistor [tolerance=±5% resistance=10k package="1206 [SMD]"]
  R2 = Resistor [tolerance=±5% resistance=10k package="1206 [SMD]"]
  C3 = Ceramic Capacitor [capacitance=100nF package="1206 [SMD, multilayer]"]
  C5 = Ceramic Capacitor [capacitance=100nF package="1206 [SMD, multilayer]"]
  C6 = Ceramic Capacitor [capacitance=4.7µF package="1206 [SMD, multilayer]"]
  C7 = Ceramic Capacitor [capacitance=4.7µF package="1206 [SMD, multilayer]"]
  I2C = female pin header, 2 pins [form="♀ (female)"]
  Reset = Pushbutton [package="[THT]"]
  SPI = female pin header, 5 pins [form="♀ (female)"]
  SEC_GND = screw terminal, 4 pins
  HTU21D = HTU21D [form="♀ (female)" package=THT]
  C8 = Ceramic Capacitor [capacitance=100nF package="1206 [SMD, multilayer]"]

nets:
  N1: A_OUT.pin1, DAC.3
  N2: A_OUT.pin2, DAC.14
  N3: A_OUT.pin3, DAC.11
  N4: A_OUT.pin4, DAC.6
  N5: A_OUT.pin7, DAC.1, DAC.2, DAC.13, Part3.5V, C3.1, C6.1
  3V3: A_OUT.pin8, CDC.8, DAC.4, Part3.3V3, C1.0, C2.+, R1.Pin_0, R2.Pin_0, C5.1, C7.1, HTU21D.VDD, C8.0
  N6: A_OUT.pin9, DAC.16
  GND: A_OUT.pin10, CDC.7, DAC.7, DAC.15, Part3.GND, C1.1, C2.-, C3.0, C5.0, C6.0, C7.0, Reset.Pin_3, Reset.Pin_4, SEC_GND.pin1, SEC_GND.pin2, SEC_GND.pin3, SEC_GND.pin4, HTU21D.GND, C8.1
  GND_2: CDC.1, Ch_1.GND, Ch_3.GND, Ch_0.GND, Ch_2.GND
  N7: CDC.2, Ch_0.OUT
  N8: CDC.3, Ch_1.OUT
  N9: CDC.4, Ch_2.OUT
  N10: CDC.5, Ch_3.OUT
  N11: CDC.9, Part3.A5/SCL, R1.Pin_1, I2C.pin1, HTU21D.SCK
  N12: CDC.10, Part3.A4/SDA, R2.Pin_1, I2C.pin2, HTU21D.DATA
  N13: DAC.8, Part3.D11_PWM/MOSI, SPI.pin3
  N14: DAC.9, Part3.D10_PWM/SS, SPI.pin2
  N15: DAC.10, Part3.D13/SCK, SPI.pin5
  N16: DAC.12, Part3.D9_PWM, SPI.pin1
  N17: Part3.D12/MISO, SPI.pin4
  N18: Part3.RESET, Reset.Pin_1, Reset.Pin_2

notes:
  N.C. A3 - A0
  N.C. 5,3.3,ref,GND
  . . . . 1
  6 . . . .
  SCL
  SDA
  SCK
  MISO
  MOSI
  SS
  LDAC
  Austin Downey
  Jan 2016 - 4Ch CapDAQ
  0.0.0.1a

custom parts:
  Locking shrouded header - 10 pins - AMP: TE Connectivity AMP Connectors 5499922-1
  FDC1004: Capacitive sensing with grounded capacitor sensors
  MAX5134: pin-compatible and software-compatible 16-bit DAC
  SMA: TE Connectivity AMP Connectors 5-1814832-1
  HTU21D: The HTU21D(F) is a new digital humidity sensor with temperature output by MEAS. Setting new standards in terms of size and intelligence, it is embedded in a reflow solderable Dual Flat No leads (DFN) package with a small 3 x 3 x 0.9 mm footprint. This sensor provides calibrated, linearized signals in digital, I²C format.
