# Fritzing sketch board 1 (saved by Fritzing 0.9.1b)
circuit board: 9cm x 6cm
breadboards: 1

parts:
  FDC1 = IC, DIP package, 10 pins [chip_label=FDC1004]
  MCP1 = MCP4922 DIP14 [chip_label=MCP4922 package="DIP (Dual Inline) [THT]"]
  MCP2 = MCP4922 DIP14 [chip_label=MCP4922 package="DIP (Dual Inline) [THT]"]
  S4 = BNC [package=bnc]
  S3 = BNC [package=bnc]
  S2 = BNC [package=bnc]
  S1 = BNC [package=bnc]
  SDA_UP = Resistor [tolerance=±5% resistance=10k package=THT]
  SCL_UP1 = Resistor [tolerance=±5% resistance=10k package=THT]
  C1 = Ceramic Capacitor [capacitance=1nF package="100 mil [THT, multilayer]"]
  C2 = Tantalum Capacitor [capacitance=1μF package="100 mil [THT, tantalum]"]
  Amp_Latch_1 = Amp-Latch connector [package="Amp Latch 10"]
  C3 = Ceramic Capacitor [capacitance=1nF package="100 mil [THT, multilayer]"]
  C4 = Tantalum Capacitor [capacitance=1μF package="100 mil [THT, tantalum]"]
  Part1 = Arduino Uno (Rev3)
  C5 = Ceramic Capacitor [capacitance=1nF package="100 mil [THT, multilayer]"]
  C6 = Tantalum Capacitor [capacitance=1μF package="100 mil [THT, tantalum]"]

nets:
  GND: FDC1.pin1, S4.GND, S3.GND, S2.GND, S1.GND
  N1: FDC1.pin2, S1.OUT
  N2: FDC1.pin3, S2.OUT
  N3: FDC1.pin4, S3.OUT
  N4: FDC1.pin5, S4.OUT
  GND_2: FDC1.pin7, MCP1.pin8, MCP1.pin12, MCP2.pin8, MCP2.pin12, C1.1, C2.-, Amp_Latch_1.10, C3.1, C4.-, Part1.GND, C5.0, C6.-
  N5: FDC1.pin8, SDA_UP.Pin_0, SCL_UP1.Pin_0, C1.0, C2.+, Part1.3V3
  N6: FDC1.pin9, SCL_UP1.Pin_1, Part1.A5/SCL
  N7: FDC1.pin10, SDA_UP.Pin_1, Part1.A4/SDA
  N8: MCP1.pin1, MCP1.pin9, MCP1.pin11, MCP1.pin13, MCP2.pin1, MCP2.pin9, MCP2.pin11, MCP2.pin13, C3.0, C4.+, Part1.5V, C5.1, C6.+
  N9: MCP1.pin3, Part1.D10_PWM/SS
  N10: MCP1.pin4, MCP2.pin4, Part1.D13/SCK
  N11: MCP1.pin5, MCP2.pin5, Part1.D11_PWM/MOSI
  N12: MCP1.pin10, Amp_Latch_1.2
  N13: MCP1.pin14, Amp_Latch_1.1
  N14: MCP2.pin3, Part1.D9_PWM
  N15: MCP2.pin10, Amp_Latch_1.4
  N16: MCP2.pin14, Amp_Latch_1.3

custom parts:
  MCP4922 DIP14: The MCP4922 device is a dual 12-bit buffered voltage output Digital-to-Analog Converters (DACs).
  BNC: BNC Connector, TE Connectivity AMP Connectors 5227161-2 Digikey number A32245-ND
  Amp-Latch connector: AMP Latch 5013308-1
